# Fritzing sketch ArduinoWebServerTemperatureSensor (saved by Fritzing 0.7.12b)
breadboards: 1

parts:
  Arduino1 = Arduino
  R1 = 4.7k Ω Resistor [package=THT]

nets:
  N1: Arduino1.D3, R1.Pin_1
  N2: Arduino1.+5V, R1.Pin_0

notes:
  leads from sensor
